# Fritzing sketch circuit (saved by Fritzing 0.9.3b)
breadboards: 3

parts:
  Part1 = Arduino Leonardo (Rev3b)
  S1 = Pushbutton [package="[THT]"]
  S2 = Pushbutton [package="[THT]"]
  S13 = Pushbutton [package="[THT]"]
  S19 = Pushbutton [package="[THT]"]
  S25 = Pushbutton [package="[THT]"]
  S31 = Pushbutton [package="[THT]"]
  S37 = Pushbutton [package="[THT]"]
  S43 = Pushbutton [package="[THT]"]
  S49 = Pushbutton [package="[THT]"]
  S51 = Pushbutton [package="[THT]"]
  S57 = Pushbutton [package="[THT]"]
  S58 = Pushbutton [package="[THT]"]
  S59 = Pushbutton [package="[THT]"]
  S60 = Pushbutton [package="[THT]"]
  S61 = Pushbutton [package="[THT]"]
  S62 = Pushbutton [package="[THT]"]
  S63 = Pushbutton [package="[THT]"]
  S64 = Pushbutton [package="[THT]"]
  S65 = Pushbutton [package="[THT]"]
  S66 = Pushbutton [package="[THT]"]
  S67 = Pushbutton [package="[THT]"]
  S68 = Pushbutton [package="[THT]"]
  LCD1 = LCD screen
  R1 = Rotary Potentiometer (Small) [maximum_resistance=100kΩ package=THT]
  R5 = Resistor [tolerance=±5% resistance=220 package=THT]
  R6 = Resistor [tolerance=±5% resistance=220 package=THT]
  R13 = Resistor [tolerance=±5% resistance=220 package=THT]
  R22 = Resistor [tolerance=±5% resistance=220 package=THT]
  R24 = Resistor [tolerance=±5% resistance=220 package=THT]
  R25 = Resistor [tolerance=±5% resistance=220 package=THT]
  R26 = Resistor [tolerance=±5% resistance=220 package=THT]
  R27 = Resistor [tolerance=±5% resistance=220 package=THT]
  R28 = Resistor [tolerance=±5% resistance=220 package=THT]
  R29 = Resistor [tolerance=±5% resistance=220 package=THT]
  R30 = Resistor [tolerance=±5% resistance=220 package=THT]
  R31 = Resistor [tolerance=±5% resistance=220 package=THT]
  R32 = Resistor [tolerance=±5% resistance=220 package=THT]
  R33 = Resistor [tolerance=±5% resistance=220 package=THT]
  R34 = Resistor [tolerance=±5% resistance=220 package=THT]
  R35 = Resistor [tolerance=±5% resistance=220 package=THT]
  R36 = Resistor [tolerance=±5% resistance=220 package=THT]
  R37 = Resistor [tolerance=±5% resistance=220 package=THT]
  R38 = Resistor [tolerance=±5% resistance=220 package=THT]
  R39 = Resistor [tolerance=±5% resistance=220 package=THT]
  R40 = Resistor [tolerance=±5% resistance=220 package=THT]
  R41 = Resistor [tolerance=±5% resistance=220 package=THT]
  R42 = Resistor [tolerance=±5% resistance=220 package=THT]
  R43 = Resistor [tolerance=±5% resistance=220 package=THT]
  R44 = Trimmer Potentiometer [maximum_resistance=10kΩ package=THT]
  R45 = Resistor [tolerance=±5% resistance=220 package=THT]
  R46 = Rotary Potentiometer (Small) [maximum_resistance=100kΩ package=THT]
  S69 = Pushbutton [package="[THT]"]
  S70 = Pushbutton [package="[THT]"]
  S71 = Pushbutton [package="[THT]"]
  S72 = Pushbutton [package="[THT]"]
  S73 = Pushbutton [package="[THT]"]
  S74 = Pushbutton [package="[THT]"]
  S75 = Pushbutton [package="[THT]"]
  S76 = Pushbutton [package="[THT]"]
  S77 = Pushbutton [package="[THT]"]
  S78 = Pushbutton [package="[THT]"]
  S79 = Pushbutton [package="[THT]"]
  S80 = Pushbutton [package="[THT]"]
  R47 = Resistor [tolerance=±5% resistance=220 package=THT]
  R48 = Resistor [tolerance=±5% resistance=220 package=THT]
  R49 = Resistor [tolerance=±5% resistance=220 package=THT]
  R50 = Resistor [tolerance=±5% resistance=220 package=THT]
  R51 = Resistor [tolerance=±5% resistance=220 package=THT]
  R52 = Resistor [tolerance=±5% resistance=220 package=THT]
  R53 = Resistor [tolerance=±5% resistance=220 package=THT]
  R54 = Resistor [tolerance=±5% resistance=220 package=THT]
  R55 = Resistor [tolerance=±5% resistance=220 package=THT]
  R56 = Resistor [tolerance=±5% resistance=220 package=THT]
  R57 = Resistor [tolerance=±5% resistance=220 package=THT]
  R58 = Resistor [tolerance=±5% resistance=220 package=THT]

nets:
  N1: Part1.D0/RX, S1.Pin_1, S1.Pin_2, R39.Pin_1, S80.Pin_1, S80.Pin_2, R47.Pin_1
  N2: Part1.D1/TX, S61.Pin_1, S61.Pin_2, R38.Pin_1, S79.Pin_1, S79.Pin_2, R48.Pin_1
  N3: Part1.D2/SDA, S58.Pin_1, S58.Pin_2, R43.Pin_1
  N4: Part1.D3_PWM/SCL, S66.Pin_1, S66.Pin_2, R42.Pin_1
  N5: Part1.D5_PWM, S59.Pin_1, S59.Pin_2, R40.Pin_1
  5V: Part1.5V, S1.Pin_3, S1.Pin_4, S57.Pin_3, S57.Pin_4, S58.Pin_3, S58.Pin_4, S59.Pin_3, S59.Pin_4, S60.Pin_3, S60.Pin_4, S61.Pin_3, S61.Pin_4, S64.Pin_3, S64.Pin_4, S66.Pin_3, S66.Pin_4, LCD1.VDD, R1.leg2, R13.Pin_1, R35.Pin_1, R44.leg1, R45.Pin_1, R46.leg2, S75.Pin_3, S75.Pin_4, S79.Pin_3, S79.Pin_4, S80.Pin_3, S80.Pin_4, R57.Pin_1
  GND: Part1.GND, LCD1.VSS, LCD1.R/W, LCD1.LED-, R1.leg1, R5.Pin_1, R6.Pin_0, R22.Pin_0, R24.Pin_1, R38.Pin_0, R39.Pin_0, R40.Pin_0, R41.Pin_0, R42.Pin_0, R43.Pin_0, R44.leg2, R46.leg1, R47.Pin_0, R48.Pin_0, R49.Pin_0
  N6: Part1.A0, R1.wiper, R46.wiper
  N7: Part1.A1, S60.Pin_1, S60.Pin_2, S62.Pin_1, S62.Pin_2, S63.Pin_1, S63.Pin_2, S65.Pin_1, S65.Pin_2, S67.Pin_1, S67.Pin_2, S68.Pin_1, S68.Pin_2, R22.Pin_1
  N8: Part1.A2, S2.Pin_1, S2.Pin_2, S13.Pin_1, S13.Pin_2, S19.Pin_1, S19.Pin_2, S25.Pin_1, S25.Pin_2, S31.Pin_1, S31.Pin_2, S37.Pin_1, S37.Pin_2, S43.Pin_1, S43.Pin_2, S49.Pin_1, S49.Pin_2, S51.Pin_1, S51.Pin_2, S57.Pin_1, S57.Pin_2, R24.Pin_0, S69.Pin_1, S69.Pin_2, S70.Pin_1, S70.Pin_2, S71.Pin_1, S71.Pin_2, S72.Pin_1, S72.Pin_2, S73.Pin_1, S73.Pin_2, S74.Pin_1, S74.Pin_2, S75.Pin_1, S75.Pin_2, S76.Pin_1, S76.Pin_2, S77.Pin_1, S77.Pin_2, S78.Pin_1, S78.Pin_2
  N9: Part1.D8/A8, LCD1.RS
  N10: Part1.D9_PWM/A9, LCD1.E
  N11: Part1.D10_PWM/A10, LCD1.DB4
  N12: Part1.D11_PWM, LCD1.DB5
  N13: Part1.D12/A11, LCD1.DB6
  N14: Part1.D13_PWM, LCD1.DB7
  N15: S2.Pin_3, S2.Pin_4, R6.Pin_1, R32.Pin_0, S71.Pin_3, S71.Pin_4, R49.Pin_1, R54.Pin_0
  N16: S13.Pin_3, S13.Pin_4, R31.Pin_0, R32.Pin_1, S73.Pin_3, S73.Pin_4, R50.Pin_0, R54.Pin_1
  N17: S19.Pin_3, S19.Pin_4, R30.Pin_0, R31.Pin_1, S72.Pin_3, S72.Pin_4, R50.Pin_1, R53.Pin_0
  N18: S25.Pin_3, S25.Pin_4, R29.Pin_0, R30.Pin_1, S69.Pin_3, S69.Pin_4, R51.Pin_0, R53.Pin_1
  N19: S31.Pin_3, S31.Pin_4, R28.Pin_0, R29.Pin_1, S70.Pin_3, S70.Pin_4, R51.Pin_1, R52.Pin_0
  N20: S37.Pin_3, S37.Pin_4, R27.Pin_0, R28.Pin_1, S76.Pin_3, S76.Pin_4, R52.Pin_1, R55.Pin_0
  N21: S43.Pin_3, S43.Pin_4, R26.Pin_0, R27.Pin_1, S78.Pin_3, S78.Pin_4, R55.Pin_1, R58.Pin_0
  N22: S49.Pin_3, S49.Pin_4, R25.Pin_0, R26.Pin_1, S77.Pin_3, S77.Pin_4, R56.Pin_0, R58.Pin_1
  N23: S51.Pin_3, S51.Pin_4, R13.Pin_0, R25.Pin_1, S74.Pin_3, S74.Pin_4, R56.Pin_1, R57.Pin_0
  N24: S62.Pin_3, S62.Pin_4, R34.Pin_0, R36.Pin_1
  N25: S63.Pin_3, S63.Pin_4, R5.Pin_0, R37.Pin_0
  N26: S64.Pin_1, S64.Pin_2, R41.Pin_1
  N27: S65.Pin_3, S65.Pin_4, R33.Pin_1, R36.Pin_0
  N28: S67.Pin_3, S67.Pin_4, R33.Pin_0, R37.Pin_1
  N29: S68.Pin_3, S68.Pin_4, R34.Pin_1, R35.Pin_0
  N30: LCD1.V0, R44.wiper
  N31: LCD1.LED+, R45.Pin_0

notes:
  length
  top:
  - k s t n h m y r w (pitch -, pitch +)
  bottom:
  a i u e o - ゛ ゜ +y submit
  blue: length
  orange: consonant
  green: vowel
  purple: lcd panel data
  grey: other
